// Digital circuit not_neg.dig as structural Verilog
module not_neg (
  input  [3:0] a,
  input  invert,
  input  neg,
  output y,
  output [3:0] cry
);

  wire and_1_out;
  wire [3:0] xor_1_out;

  xor xor_1 (xor_1_out[3], invert, a[3]);
  xor xor_2 (xor_1_out[2], invert, a[2]);
  xor xor_3 (xor_1_out[1], invert, a[1]);
  xor xor_4 (xor_1_out[0], invert, a[0]);
  and and_1 (and_1_out, invert, neg);
  // incrementer incrementer_1: pin names not known; wires that end beside it: xor_1_out, and_1_out, y, cry
endmodule
